# Fritzing sketch Helicopter Prototype Circuit (saved by Fritzing 0.9.2b)
breadboards: 1

parts:
  IC2 = IC, DIP package, 14 pins [chip_label="QUAD OR"]
  IC3 = IC, DIP package, 14 pins [chip_label="QUAD XOR"]
  Part1 = Arduino Uno (Rev3)
  IC1 = IC, DIP package, 14 pins [chip_label=DAC]  # not connected
  C1 = Ceramic Capacitor [capacitance=10pF package="100 mil [THT, multilayer]"]
  C2 = Ceramic Capacitor [capacitance=100nF package="100 mil [THT, multilayer]"]
  R2 = Resistor [tolerance=±5% resistance=220 package=THT]
  R3 = Resistor [tolerance=±5% resistance=220 package=THT]

nets:
  N1: IC2.pin7, IC3.pin7, Part1.5V
  N2: IC2.pin8, IC3.pin10
  N3: IC2.pin9, IC3.pin13
  N4: IC2.pin10, Part1.D2
  N5: IC2.pin14, IC3.pin14, Part1.GND, C1.0, C2.0
  N6: IC3.pin8, C2.1, R3.Pin_0
  N7: IC3.pin9, R3.Pin_1
  N8: IC3.pin11, C1.1, R2.Pin_0
  N9: IC3.pin12, R2.Pin_1
